// Logisim project RGLED.circ as structural Verilog
// LED计数
module \LED计数电路  (
  input  in_1,
  input  in_2,
  input  in_3,
  input  in_4,
  input  in_5,
  output out_6,
  output out_7,
  output out_8,
  output out_9,
  output out_10
);

  or or_1 (out_6, in_1, in_2, in_3, in_4, in_5);
  or or_2 (out_7, in_2, in_3, in_4, in_5);
  or or_3 (out_8, in_3, in_4, in_5);
  or or_4 (out_9, in_4, in_5);

  assign out_10 = in_5;
endmodule

module \数码管驱动  (
  input  X3,
  input  X2,
  input  X1,
  input  X0,
  output Seg_1,
  output Seg_2,
  output Seg_3,
  output Seg_4,
  output Seg_5,
  output Seg_6,
  output Seg_7
);

  wire and_1_out, and_2_out, and_3_out, and_4_out, and_5_out, and_6_out, and_7_out, and_8_out, and_9_out,
       and_10_out, and_11_out, and_12_out, and_13_out, and_14_out, and_15_out, and_16_out, not_1_out,
       not_2_out, not_3_out, not_4_out, not_5_out, not_6_out, not_7_out, not_8_out, not_9_out, not_10_out,
       not_11_out, not_12_out, not_13_out, not_14_out, not_15_out, not_16_out, not_17_out, not_18_out,
       not_19_out, not_20_out, not_21_out;

  not not_1 (not_1_out, X2);
  and and_1 (and_1_out, not_1_out, X1);
  and and_2 (and_2_out, X2, not_2_out);
  not not_2 (not_2_out, X1);
  and and_3 (and_3_out, X2, not_3_out);
  not not_3 (not_3_out, X0);
  not not_4 (not_4_out, X1);
  and and_4 (and_4_out, not_4_out, not_5_out);
  not not_5 (not_5_out, X0);
  and and_5 (and_5_out, X2, not_6_out);
  not not_6 (not_6_out, X1);
  and and_6 (and_6_out, X2, not_7_out);
  not not_7 (not_7_out, X0);
  not not_8 (not_8_out, X2);
  and and_7 (and_7_out, not_8_out, not_9_out);
  not not_9 (not_9_out, X0);
  and and_8 (and_8_out, X2, X0);
  not not_10 (not_10_out, X2);
  not not_11 (not_11_out, X1);
  and and_9 (and_9_out, not_11_out, not_12_out);
  not not_12 (not_12_out, X0);
  and and_10 (and_10_out, X1, X0);
  not not_13 (not_13_out, X2);
  and and_11 (and_11_out, not_13_out, not_14_out);
  not not_14 (not_14_out, X0);
  and and_12 (and_12_out, X1, not_15_out);
  not not_15 (not_15_out, X0);
  not not_16 (not_16_out, X2);
  and and_13 (and_13_out, not_16_out, not_17_out);
  not not_17 (not_17_out, X0);
  not not_18 (not_18_out, X2);
  and and_14 (and_14_out, not_18_out, X1);
  and and_15 (and_15_out, X1, not_19_out);
  not not_19 (not_19_out, X0);
  not not_20 (not_20_out, X1);
  and and_16 (and_16_out, X2, not_20_out, X0);
  not not_21 (not_21_out, X1);
  or or_1 (Seg_7, not_21_out, X0, X2);
  or or_2 (Seg_1, and_1_out, and_2_out, and_3_out, X3);
  or or_3 (Seg_2, and_4_out, and_5_out, and_6_out, X3);
  or or_4 (Seg_3, and_7_out, X1, and_8_out, X3);
  or or_5 (Seg_4, not_10_out, and_9_out, and_10_out);
  or or_6 (Seg_5, and_11_out, and_12_out);
  or or_7 (Seg_6, and_13_out, and_14_out, and_15_out, and_16_out, X3);
endmodule

module \数码管驱动测试  (
);

  wire clock_1_out, \数码管驱动_1_seg_1 , \数码管驱动_1_seg_2 , \数码管驱动_1_seg_3 , \数码管驱动_1_seg_4 , \数码管驱动_1_seg_5 ,
       \数码管驱动_1_seg_6 , \数码管驱动_1_seg_7 ;
  wire [3:0] counter_1_q;

  Counter #(.width(4), .max('hf), .ongoal("wrap"), .trigger("rising"), .behavior("old")) counter_1 (
    .Q(counter_1_q), .clk(clock_1_out));  // open: load, D, count, carry, clr, preset
  Clock #(.highDuration(1), .lowDuration(1)) clock_1 (.out(clock_1_out));
  \数码管驱动  \u_数码管驱动_1  (
    .X3(counter_1_q[3]), .X2(counter_1_q[2]), .Seg_1(\数码管驱动_1_seg_1 ), .X1(counter_1_q[1]),
    .X0(counter_1_q[0]), .Seg_2(\数码管驱动_1_seg_2 ), .Seg_3(\数码管驱动_1_seg_3 ), .Seg_4(\数码管驱动_1_seg_4 ),
    .Seg_5(\数码管驱动_1_seg_5 ), .Seg_6(\数码管驱动_1_seg_6 ), .Seg_7(\数码管驱动_1_seg_7 ));
  _7_Segment_Display #(.active("true")) u_7_segment_display_1 (
    .g(\数码管驱动_1_seg_1 ), .f(\数码管驱动_1_seg_2 ), .a(\数码管驱动_1_seg_3 ), .b(\数码管驱动_1_seg_4 ), .e(\数码管驱动_1_seg_5 ),
    .d(\数码管驱动_1_seg_6 ), .c(\数码管驱动_1_seg_7 ));  // open: dp

  // Notes on the sheet:
  //   Ctrl+T驱动时钟单步运行测试
endmodule

// 4位数比较器
module \_4位无符号比较器  (
  input  X3,
  input  X2,
  input  X1,
  input  X0,
  input  Y3,
  input  Y2,
  input  Y1,
  input  Y0,
  output Great,
  output Equal,
  output Less
);

  wire and_1_out, and_2_out, and_3_out, and_4_out, and_5_out, and_6_out, and_7_out, and_8_out, and_9_out,
       and_10_out, and_11_out, and_12_out, and_13_out, and_14_out, and_15_out, and_16_out, and_17_out,
       and_18_out, and_19_out, and_20_out, and_21_out, and_22_out, and_23_out, and_24_out, and_25_out,
       and_26_out, and_27_out, and_28_out, and_29_out, and_30_out, and_31_out, and_32_out, and_33_out,
       and_34_out, and_35_out, and_36_out, and_37_out, and_38_out, and_39_out, and_40_out, and_41_out,
       and_42_out, and_43_out, and_44_out, and_45_out, and_46_out, not_1_out, not_2_out, not_3_out,
       not_4_out, not_5_out, not_6_out, not_7_out, not_8_out, not_9_out, not_10_out, not_11_out, not_12_out,
       not_13_out, not_14_out, not_15_out, not_16_out, not_17_out, not_18_out, not_19_out, not_20_out,
       not_21_out, not_22_out, not_23_out, not_24_out, not_25_out, not_26_out, not_27_out, not_28_out,
       not_29_out, not_30_out, not_31_out, not_32_out, not_33_out, not_34_out, not_35_out, not_36_out,
       not_37_out, not_38_out, not_39_out, not_40_out, not_41_out, not_42_out, not_43_out, not_44_out,
       not_45_out, not_46_out, not_47_out, not_48_out, not_49_out, not_50_out, not_51_out, not_52_out,
       not_53_out, not_54_out, not_55_out, not_56_out, not_57_out, not_58_out, not_59_out, not_60_out,
       not_61_out, not_62_out, not_63_out, not_64_out, not_65_out, not_66_out, not_67_out, not_68_out,
       not_69_out, not_70_out, not_71_out, not_72_out, not_73_out, not_74_out, not_75_out, not_76_out,
       not_77_out, not_78_out, not_79_out, not_80_out, not_81_out, not_82_out, not_83_out, not_84_out,
       not_85_out, not_86_out, not_87_out, not_88_out, not_89_out, not_90_out, not_91_out, not_92_out,
       not_93_out, not_94_out, not_95_out, not_96_out, not_97_out, not_98_out, not_99_out, not_100_out,
       not_101_out, not_102_out, not_103_out, not_104_out, not_105_out, not_106_out, not_107_out,
       not_108_out, not_109_out, not_110_out, not_111_out, not_112_out, not_113_out, not_114_out,
       not_115_out, not_116_out, not_117_out, not_118_out, not_119_out, not_120_out, not_121_out,
       not_122_out, not_123_out, not_124_out, not_125_out, not_126_out, not_127_out, not_128_out;

  not not_1 (not_1_out, Y3);
  not not_2 (not_2_out, Y2);
  not not_3 (not_3_out, Y1);
  not not_4 (not_4_out, Y0);
  not not_5 (not_5_out, Y3);
  not not_6 (not_6_out, Y2);
  not not_7 (not_7_out, Y1);
  not not_8 (not_8_out, Y3);
  not not_9 (not_9_out, Y2);
  not not_10 (not_10_out, Y0);
  not not_11 (not_11_out, Y3);
  not not_12 (not_12_out, Y2);
  not not_13 (not_13_out, Y3);
  not not_14 (not_14_out, Y1);
  not not_15 (not_15_out, Y0);
  not not_16 (not_16_out, Y3);
  not not_17 (not_17_out, Y1);
  not not_18 (not_18_out, Y3);
  not not_19 (not_19_out, Y0);
  not not_20 (not_20_out, Y3);
  not not_21 (not_21_out, Y2);
  not not_22 (not_22_out, Y1);
  not not_23 (not_23_out, Y0);
  not not_24 (not_24_out, Y2);
  not not_25 (not_25_out, Y1);
  not not_26 (not_26_out, Y2);
  not not_27 (not_27_out, Y0);
  not not_28 (not_28_out, Y2);
  not not_29 (not_29_out, Y1);
  not not_30 (not_30_out, Y0);
  not not_31 (not_31_out, Y1);
  not not_32 (not_32_out, Y0);
  not not_33 (not_33_out, X3);
  not not_34 (not_34_out, X2);
  not not_35 (not_35_out, X1);
  not not_36 (not_36_out, X0);
  not not_37 (not_37_out, Y3);
  not not_38 (not_38_out, Y2);
  not not_39 (not_39_out, Y1);
  not not_40 (not_40_out, Y0);
  not not_41 (not_41_out, X3);
  not not_42 (not_42_out, X2);
  not not_43 (not_43_out, X1);
  not not_44 (not_44_out, Y3);
  not not_45 (not_45_out, Y2);
  not not_46 (not_46_out, Y1);
  not not_47 (not_47_out, X3);
  not not_48 (not_48_out, X2);
  not not_49 (not_49_out, X0);
  not not_50 (not_50_out, Y3);
  not not_51 (not_51_out, Y2);
  not not_52 (not_52_out, Y0);
  not not_53 (not_53_out, X3);
  not not_54 (not_54_out, X2);
  not not_55 (not_55_out, Y3);
  not not_56 (not_56_out, Y2);
  not not_57 (not_57_out, X3);
  not not_58 (not_58_out, X1);
  not not_59 (not_59_out, X0);
  not not_60 (not_60_out, Y3);
  not not_61 (not_61_out, Y1);
  not not_62 (not_62_out, Y0);
  not not_63 (not_63_out, X3);
  not not_64 (not_64_out, X1);
  not not_65 (not_65_out, Y3);
  not not_66 (not_66_out, Y1);
  not not_67 (not_67_out, X3);
  not not_68 (not_68_out, X0);
  not not_69 (not_69_out, Y3);
  not not_70 (not_70_out, Y0);
  not not_71 (not_71_out, X3);
  not not_72 (not_72_out, Y3);
  not not_73 (not_73_out, X2);
  not not_74 (not_74_out, X1);
  not not_75 (not_75_out, X0);
  not not_76 (not_76_out, Y2);
  not not_77 (not_77_out, Y1);
  not not_78 (not_78_out, Y0);
  not not_79 (not_79_out, X2);
  not not_80 (not_80_out, X1);
  not not_81 (not_81_out, Y2);
  not not_82 (not_82_out, Y1);
  not not_83 (not_83_out, X2);
  not not_84 (not_84_out, X0);
  not not_85 (not_85_out, Y2);
  not not_86 (not_86_out, Y0);
  not not_87 (not_87_out, X2);
  not not_88 (not_88_out, Y2);
  not not_89 (not_89_out, X1);
  not not_90 (not_90_out, X0);
  not not_91 (not_91_out, Y1);
  not not_92 (not_92_out, Y0);
  not not_93 (not_93_out, X1);
  not not_94 (not_94_out, Y1);
  not not_95 (not_95_out, X0);
  not not_96 (not_96_out, Y0);
  not not_97 (not_97_out, X3);
  not not_98 (not_98_out, X2);
  not not_99 (not_99_out, X1);
  not not_100 (not_100_out, X0);
  not not_101 (not_101_out, X3);
  not not_102 (not_102_out, X2);
  not not_103 (not_103_out, X1);
  not not_104 (not_104_out, X3);
  not not_105 (not_105_out, X2);
  not not_106 (not_106_out, X0);
  not not_107 (not_107_out, X3);
  not not_108 (not_108_out, X2);
  not not_109 (not_109_out, X3);
  not not_110 (not_110_out, X1);
  not not_111 (not_111_out, X0);
  not not_112 (not_112_out, X3);
  not not_113 (not_113_out, X1);
  not not_114 (not_114_out, X3);
  not not_115 (not_115_out, X0);
  not not_116 (not_116_out, X3);
  not not_117 (not_117_out, X2);
  not not_118 (not_118_out, X1);
  not not_119 (not_119_out, X0);
  not not_120 (not_120_out, X2);
  not not_121 (not_121_out, X1);
  not not_122 (not_122_out, X2);
  not not_123 (not_123_out, X0);
  not not_124 (not_124_out, X2);
  not not_125 (not_125_out, X1);
  not not_126 (not_126_out, X0);
  not not_127 (not_127_out, X1);
  not not_128 (not_128_out, X0);
  and and_1 (and_1_out, X0, not_1_out, not_2_out, not_3_out, not_4_out);
  and and_2 (and_2_out, X1, not_5_out, not_6_out, not_7_out);
  and and_3 (and_3_out, X1, X0, not_8_out, not_9_out, not_10_out);
  and and_4 (and_4_out, X2, not_11_out, not_12_out);
  and and_5 (and_5_out, X2, X0, not_13_out, not_14_out, not_15_out);
  and and_6 (and_6_out, X2, X1, not_16_out, not_17_out);
  and and_7 (and_7_out, X2, X1, X0, not_18_out, not_19_out);
  and and_8 (and_8_out, X3, not_20_out);
  and and_9 (and_9_out, X3, X0, not_21_out, not_22_out, not_23_out);
  and and_10 (and_10_out, X3, X1, not_24_out, not_25_out);
  and and_11 (and_11_out, X3, X1, X0, not_26_out, not_27_out);
  and and_12 (and_12_out, X3, X2, not_28_out);
  and and_13 (and_13_out, X3, X2, X0, not_29_out, not_30_out);
  and and_14 (and_14_out, X3, X2, X1, not_31_out);
  and and_15 (and_15_out, X3, X2, X1, X0, not_32_out);
  and and_16 (and_16_out, not_33_out, not_34_out, not_35_out, not_36_out, not_37_out, not_38_out, not_39_out, not_40_out);
  and and_17 (and_17_out, not_41_out, not_42_out, not_43_out, X0, not_44_out, not_45_out, not_46_out, Y0);
  and and_18 (and_18_out, not_47_out, not_48_out, X1, not_49_out, not_50_out, not_51_out, Y1, not_52_out);
  and and_19 (and_19_out, not_53_out, not_54_out, X1, X0, not_55_out, not_56_out, Y1, Y0);
  and and_20 (and_20_out, not_57_out, X2, not_58_out, not_59_out, not_60_out, Y2, not_61_out, not_62_out);
  and and_21 (and_21_out, not_63_out, X2, not_64_out, X0, not_65_out, Y2, not_66_out, Y0);
  and and_22 (and_22_out, not_67_out, X2, X1, not_68_out, not_69_out, Y2, Y1, not_70_out);
  and and_23 (and_23_out, not_71_out, X2, X1, X0, not_72_out, Y2, Y1, Y0);
  and and_24 (and_24_out, X3, not_73_out, not_74_out, not_75_out, Y3, not_76_out, not_77_out, not_78_out);
  and and_25 (and_25_out, X3, not_79_out, not_80_out, X0, Y3, not_81_out, not_82_out, Y0);
  and and_26 (and_26_out, X3, not_83_out, X1, not_84_out, Y3, not_85_out, Y1, not_86_out);
  and and_27 (and_27_out, X3, not_87_out, X1, X0, Y3, not_88_out, Y1, Y0);
  and and_28 (and_28_out, X3, X2, not_89_out, not_90_out, Y3, Y2, not_91_out, not_92_out);
  and and_29 (and_29_out, X3, X2, not_93_out, X0, Y3, Y2, not_94_out, Y0);
  and and_30 (and_30_out, X3, X2, X1, not_95_out, Y3, Y2, Y1, not_96_out);
  and and_31 (and_31_out, X3, X2, X1, X0, Y3, Y2, Y1, Y0);
  and and_32 (and_32_out, not_97_out, not_98_out, not_99_out, not_100_out, Y0);
  and and_33 (and_33_out, not_101_out, not_102_out, not_103_out, Y1);
  and and_34 (and_34_out, not_104_out, not_105_out, not_106_out, Y1, Y0);
  and and_35 (and_35_out, not_107_out, not_108_out, Y2);
  and and_36 (and_36_out, not_109_out, not_110_out, not_111_out, Y2, Y0);
  and and_37 (and_37_out, not_112_out, not_113_out, Y2, Y1);
  and and_38 (and_38_out, not_114_out, not_115_out, Y2, Y1, Y0);
  and and_39 (and_39_out, not_116_out, Y3);
  and and_40 (and_40_out, not_117_out, not_118_out, not_119_out, Y3, Y0);
  and and_41 (and_41_out, not_120_out, not_121_out, Y3, Y1);
  and and_42 (and_42_out, not_122_out, not_123_out, Y3, Y1, Y0);
  and and_43 (and_43_out, not_124_out, Y3, Y2);
  and and_44 (and_44_out, not_125_out, not_126_out, Y3, Y2, Y0);
  and and_45 (and_45_out, not_127_out, Y3, Y2, Y1);
  and and_46 (and_46_out, not_128_out, Y3, Y2, Y1, Y0);
  or or_1 (Great, and_1_out, and_2_out, and_3_out, and_4_out, and_5_out, and_6_out, and_7_out, and_8_out, and_9_out, and_10_out, and_11_out, and_12_out, and_13_out, and_14_out, and_15_out);
  or or_2 (Less, and_32_out, and_33_out, and_34_out, and_35_out, and_36_out, and_37_out, and_38_out, and_39_out, and_40_out, and_41_out, and_42_out, and_43_out, and_44_out, and_45_out, and_46_out);
  or or_3 (Equal, and_16_out, and_17_out, and_18_out, and_19_out, and_20_out, and_21_out, and_22_out, and_23_out, and_24_out, and_25_out, and_26_out, and_27_out, and_28_out, and_29_out, and_30_out, and_31_out);
endmodule

module \_8位无符号比较器  (
  input  [7:0] X,
  input  [7:0] Y,
  output Great,
  output Equal,
  output Less
);

  wire and_1_out, and_2_out, \n4位无符号比较器_1_equal , \n4位无符号比较器_1_great , \n4位无符号比较器_1_less ,
       \n4位无符号比较器_2_equal , \n4位无符号比较器_2_great , \n4位无符号比较器_2_less ;

  // Probe on X
  // Probe on Y
  \_4位无符号比较器  \u_4位无符号比较器_1  (
    .X3(X[7]), .X2(X[6]), .X1(X[5]), .X0(X[4]), .Y3(Y[7]), .Y2(Y[6]), .Y1(Y[5]), .Y0(Y[4]),
    .Great(\n4位无符号比较器_1_great ), .Equal(\n4位无符号比较器_1_equal ), .Less(\n4位无符号比较器_1_less ));
  \_4位无符号比较器  \u_4位无符号比较器_2  (
    .X3(X[3]), .X2(X[2]), .X1(X[1]), .X0(X[0]), .Y3(Y[3]), .Y2(Y[2]), .Y1(Y[1]), .Y0(Y[0]),
    .Great(\n4位无符号比较器_2_great ), .Equal(\n4位无符号比较器_2_equal ), .Less(\n4位无符号比较器_2_less ));
  and and_1 (and_1_out, \n4位无符号比较器_1_equal , \n4位无符号比较器_2_great );
  and and_2 (and_2_out, \n4位无符号比较器_1_equal , \n4位无符号比较器_2_less );
  or or_1 (Great, \n4位无符号比较器_1_great , and_1_out);
  and and_3 (Equal, \n4位无符号比较器_1_equal , \n4位无符号比较器_2_equal );
  or or_2 (Less, \n4位无符号比较器_1_less , and_2_out);

  // Other names for the same wires on the sheet: X0[3:0] = X[3:0]; X1[3:0] = X[7:4]; Y0[3:0] = Y[3:0];
  //   Y1[3:0] = Y[7:4]

  // Notes on the sheet:
  //   电路功能：X,Y进行无符号比较，Great=(X>Y)?1:0;
  //   输入引脚区
  //   输出引脚区
endmodule

// MUX
module \_2路选择器_1位  (
  input  X0,
  input  Sel,
  input  X1,
  output Out
);

  wire and_1_out, and_2_out, not_1_out;

  not not_1 (not_1_out, Sel);
  and and_1 (and_1_out, X0, not_1_out);
  and and_2 (and_2_out, X1, Sel);
  or or_1 (Out, and_1_out, and_2_out);

  // Notes on the sheet:
  //   输入引脚区
  //   电路功能：Out=(Sel==0)?X0:X1;
  //   请勿增删改引脚，请在下方利用上方输入输出引脚的隧道标签信号构建电路，ctrl+d复制选择组件
  //   输出引脚区
endmodule

// MUX
module \_2路选择器_8位  (
  input  [7:0] X,
  input  Sel,
  input  [7:0] Y,
  output [7:0] Out
);

  wire [7:0] and_1_out, and_2_out, not_1_out;

  // Probe on X
  // Probe on Y
  assign and_1_out = X & not_1_out;  // AND_Gate and_1, 8 bits wide
  assign not_1_out = ~{8{Sel}};  // NOT_Gate not_1, 8 bits wide
  assign and_2_out = Y & {8{Sel}};  // AND_Gate and_2, 8 bits wide
  // Probe on Out
  assign Out = and_1_out | and_2_out;  // OR_Gate or_1, 8 bits wide

  // Notes on the sheet:
  //   输入引脚区
  //   电路功能：Out=(Sel==0)?X:Y;
  //   请勿增删改引脚，请在下方利用上方输入输出引脚的隧道标签信号构建电路，ctrl+d复制选择组件
  //   输出引脚区
endmodule

// 计数器
module \BCD双向计数器_可异步置位  (
  input  CLK,
  input  \使能 ,
  input  \异步置位控制 ,
  input  [3:0] \异步预置 ,
  input  \Mode_0正计数_1倒计数 ,
  output [3:0] \输出Q ,
  output \进位_借位 
);

  wire \bcd双向计数器状态转换_自动生成_1_n0 , \bcd双向计数器状态转换_自动生成_1_n1 , \bcd双向计数器状态转换_自动生成_1_n2 ,
       \bcd双向计数器状态转换_自动生成_1_n3 , D0, D1, D2, D3, not_1_out, not_2_out, not_3_out, not_4_out;

  \BCD双向计数器状态转换_自动生成  \bcd双向计数器状态转换_自动生成_1  (
    .S3(\输出Q [3]), .S2(\输出Q [2]), .S1(\输出Q [1]), .S0(\输出Q [0]), .N3(\bcd双向计数器状态转换_自动生成_1_n3 ),
    .Mode(\Mode_0正计数_1倒计数 ), .N2(\bcd双向计数器状态转换_自动生成_1_n2 ), .N1(\bcd双向计数器状态转换_自动生成_1_n1 ),
    .N0(\bcd双向计数器状态转换_自动生成_1_n0 ));
  \BCD双向计数器输出函数_自动生成  \bcd双向计数器输出函数_自动生成_1  (
    .S3(\输出Q [3]), .S2(\输出Q [2]), .S1(\输出Q [1]), .Cout(\进位_借位 ), .S0(\输出Q [0]), .Mode(\Mode_0正计数_1倒计数 ));
  assign {D3, D2, D1, D0} = \异步置位控制  ? \异步预置  : 4'bz;  // Controlled_Buffer controlled_buffer_1
  D_Flip_Flop #(.trigger("rising"), .Pre_Clr_Positions("LEGACY"), .NegatePresetClear("false"), .enable("true"), .NewFFLayout("false")) u_D3 (
    .clk(CLK), .D(\bcd双向计数器状态转换_自动生成_1_n3 ), .Q(\输出Q [3]), .preset(D3), .en(\使能 ), .reset(not_1_out));  // open: Qn
  not not_1 (not_1_out, D3);
  D_Flip_Flop #(.trigger("rising"), .Pre_Clr_Positions("LEGACY"), .NegatePresetClear("false"), .enable("true"), .NewFFLayout("false")) u_D2 (
    .clk(CLK), .D(\bcd双向计数器状态转换_自动生成_1_n2 ), .Q(\输出Q [2]), .preset(D2), .en(\使能 ), .reset(not_2_out));  // open: Qn
  not not_2 (not_2_out, D2);
  D_Flip_Flop #(.trigger("rising"), .Pre_Clr_Positions("LEGACY"), .NegatePresetClear("false"), .enable("true"), .NewFFLayout("false")) u_D1 (
    .clk(CLK), .D(\bcd双向计数器状态转换_自动生成_1_n1 ), .Q(\输出Q [1]), .preset(D1), .en(\使能 ), .reset(not_3_out));  // open: Qn
  not not_3 (not_3_out, D1);
  D_Flip_Flop #(.trigger("rising"), .Pre_Clr_Positions("LEGACY"), .NegatePresetClear("false"), .enable("true"), .NewFFLayout("false")) u_D0 (
    .clk(CLK), .D(\bcd双向计数器状态转换_自动生成_1_n0 ), .Q(\输出Q [0]), .preset(D0), .en(\使能 ), .reset(not_4_out));  // open: Qn
  not not_4 (not_4_out, D0);
  // Probe on \输出Q 

  // Other names for the same wires on the sheet: Cout = \进位_借位 ; Din[3:0] = \异步预置 ; En = \使能 ;
  //   Mode = \Mode_0正计数_1倒计数 ; PreSet = \异步置位控制 ; Q[3:0] = \输出Q 

  // Notes on the sheet:
  //   正计数到9，倒计数到0时输出为1
endmodule

// 状态转换
module \BCD双向计数器状态转换_自动生成  (
  input  S3,
  input  S2,
  input  S1,
  input  S0,
  input  Mode,
  output N3,
  output N2,
  output N1,
  output N0
);

  wire and_1_out, and_2_out, and_3_out, and_4_out, and_5_out, and_6_out, and_7_out, and_8_out, and_9_out,
       and_10_out, and_11_out, and_12_out, and_13_out, and_14_out, and_15_out, and_16_out, not_1_out,
       not_2_out, not_3_out, not_4_out, not_5_out, not_6_out, not_7_out, not_8_out, not_9_out, not_10_out,
       not_11_out, not_12_out, not_13_out, not_14_out, not_15_out, not_16_out, not_17_out, not_18_out,
       not_19_out, not_20_out, not_21_out, not_22_out, not_23_out, not_24_out, not_25_out, not_26_out,
       not_27_out, not_28_out, not_29_out, not_30_out, not_31_out, not_32_out, not_33_out, not_34_out,
       not_35_out, not_36_out, not_37_out, not_38_out, not_39_out, not_40_out, not_41_out, not_42_out;

  not not_1 (not_1_out, S3);
  not not_2 (not_2_out, S2);
  not not_3 (not_3_out, S1);
  not not_4 (not_4_out, S0);
  not not_5 (not_5_out, S3);
  not not_6 (not_6_out, Mode);
  not not_7 (not_7_out, S2);
  not not_8 (not_8_out, S1);
  not not_9 (not_9_out, S0);
  not not_10 (not_10_out, Mode);
  not not_11 (not_11_out, S2);
  not not_12 (not_12_out, S1);
  not not_13 (not_13_out, S3);
  not not_14 (not_14_out, S2);
  not not_15 (not_15_out, Mode);
  not not_16 (not_16_out, S3);
  not not_17 (not_17_out, S1);
  not not_18 (not_18_out, Mode);
  not not_19 (not_19_out, S3);
  not not_20 (not_20_out, S3);
  not not_21 (not_21_out, S0);
  not not_22 (not_22_out, S2);
  not not_23 (not_23_out, S1);
  not not_24 (not_24_out, S0);
  not not_25 (not_25_out, S3);
  not not_26 (not_26_out, S1);
  not not_27 (not_27_out, Mode);
  not not_28 (not_28_out, S3);
  not not_29 (not_29_out, S0);
  not not_30 (not_30_out, Mode);
  not not_31 (not_31_out, S3);
  not not_32 (not_32_out, S3);
  not not_33 (not_33_out, S1);
  not not_34 (not_34_out, S0);
  not not_35 (not_35_out, S2);
  not not_36 (not_36_out, S1);
  not not_37 (not_37_out, S0);
  not not_38 (not_38_out, S3);
  not not_39 (not_39_out, S0);
  not not_40 (not_40_out, S2);
  not not_41 (not_41_out, S1);
  not not_42 (not_42_out, S0);
  and and_1 (and_1_out, not_1_out, not_2_out, not_3_out, not_4_out, Mode);
  and and_2 (and_2_out, not_5_out, S2, S1, S0, not_6_out);
  and and_3 (and_3_out, S3, not_7_out, not_8_out, not_9_out, not_10_out);
  and and_4 (and_4_out, S3, not_11_out, not_12_out, S0, Mode);
  and and_5 (and_5_out, not_13_out, not_14_out, S1, S0, not_15_out);
  and and_6 (and_6_out, not_16_out, S2, not_17_out, not_18_out);
  and and_7 (and_7_out, not_19_out, S2, S0, Mode);
  and and_8 (and_8_out, not_20_out, S2, S1, not_21_out);
  and and_9 (and_9_out, S3, not_22_out, not_23_out, not_24_out, Mode);
  and and_10 (and_10_out, not_25_out, not_26_out, S0, not_27_out);
  and and_11 (and_11_out, not_28_out, S1, not_29_out, not_30_out);
  and and_12 (and_12_out, not_31_out, S1, S0, Mode);
  and and_13 (and_13_out, not_32_out, S2, not_33_out, not_34_out, Mode);
  and and_14 (and_14_out, S3, not_35_out, not_36_out, not_37_out, Mode);
  and and_15 (and_15_out, not_38_out, not_39_out);
  and and_16 (and_16_out, not_40_out, not_41_out, not_42_out);
  or or_1 (N3, and_1_out, and_2_out, and_3_out, and_4_out);
  or or_2 (N2, and_5_out, and_6_out, and_7_out, and_8_out, and_9_out);
  or or_3 (N1, and_10_out, and_11_out, and_12_out, and_13_out, and_14_out);
  or or_4 (N0, and_15_out, and_16_out);
endmodule

module \BCD双向计数器输出函数_自动生成  (
  input  S3,
  input  S2,
  input  S1,
  input  S0,
  input  Mode,
  output Cout
);

  wire and_1_out, and_2_out, not_1_out, not_2_out, not_3_out, not_4_out, not_5_out, not_6_out, not_7_out;

  not not_1 (not_1_out, S3);
  not not_2 (not_2_out, S2);
  not not_3 (not_3_out, S1);
  not not_4 (not_4_out, S0);
  not not_5 (not_5_out, S2);
  not not_6 (not_6_out, S1);
  not not_7 (not_7_out, Mode);
  and and_1 (and_1_out, not_1_out, not_2_out, not_3_out, not_4_out, Mode);
  and and_2 (and_2_out, S3, not_5_out, not_6_out, S0, not_7_out);
  or or_1 (Cout, and_1_out, and_2_out);
endmodule

// 倒计数
module \双位十进制双向计数器  (
  input  CLK,
  input  \使能 ,
  input  \异步置位控制 ,
  input  [7:0] \异步预置 ,
  input  \Mode_0正计数_1倒计数 ,
  output [7:0] Q,
  output \进位_借位 
);

  wire and_1_out, \bcd双向计数器_可异步置位_1_进位_借位 , \bcd双向计数器_可异步置位_2_进位_借位 ;

  \BCD双向计数器_可异步置位  \bcd双向计数器_可异步置位_1  (
    .CLK(CLK), .\使能 (\使能 ), .\异步置位控制 (\异步置位控制 ), .\异步预置 (\异步预置 [3:0]), .\Mode_0正计数_1倒计数 (\Mode_0正计数_1倒计数 ),
    .\输出Q (Q[3:0]), .\进位_借位 (\bcd双向计数器_可异步置位_1_进位_借位 ));
  and and_1 (and_1_out, \使能 , \bcd双向计数器_可异步置位_1_进位_借位 );
  \BCD双向计数器_可异步置位  \bcd双向计数器_可异步置位_2  (
    .CLK(CLK), .\使能 (and_1_out), .\异步置位控制 (\异步置位控制 ), .\异步预置 (\异步预置 [7:4]),
    .\Mode_0正计数_1倒计数 (\Mode_0正计数_1倒计数 ), .\输出Q (Q[7:4]), .\进位_借位 (\bcd双向计数器_可异步置位_2_进位_借位 ));
  and and_2 (\进位_借位 , \bcd双向计数器_可异步置位_2_进位_借位 , \bcd双向计数器_可异步置位_1_进位_借位 );
  // Probe on Q

  // Other names for the same wires on the sheet: Cout = \进位_借位 ; Din[7:0] = \异步预置 ; Din0[3:0] = \异步预置 [3:0];
  //   Din1[3:0] = \异步预置 [7:4]; En = \使能 ; Mode = \Mode_0正计数_1倒计数 ; PreSet = \异步置位控制 

  // Notes on the sheet:
  //   正计数到9，倒计数到0时输出为1
endmodule

// 状态机
module \红绿灯状态机_自动生成  (
  input  S2,
  input  S1,
  input  S0,
  input  T1,
  input  T2,
  input  T3,
  input  T4,
  input  EMERG,
  output N2,
  output N1,
  output N0
);

  wire and_1_out, and_2_out, and_3_out, and_4_out, and_5_out, and_6_out, and_7_out, and_8_out, and_9_out,
       not_1_out, not_2_out, not_3_out, not_4_out, not_5_out, not_6_out, not_7_out, not_8_out, not_9_out,
       not_10_out, not_11_out, not_12_out, not_13_out, not_14_out, not_15_out, not_16_out, not_17_out,
       not_18_out, not_19_out, not_20_out, not_21_out, not_22_out, not_23_out, not_24_out, not_25_out,
       not_26_out;

  not not_1 (not_1_out, S2);
  and and_1 (and_1_out, not_1_out, EMERG);
  not not_2 (not_2_out, S1);
  not not_3 (not_3_out, S0);
  and and_2 (and_2_out, not_2_out, not_3_out, EMERG);
  not not_4 (not_4_out, S2);
  not not_5 (not_5_out, S1);
  not not_6 (not_6_out, EMERG);
  not not_7 (not_7_out, S2);
  not not_8 (not_8_out, S0);
  not not_9 (not_9_out, EMERG);
  not not_10 (not_10_out, S2);
  not not_11 (not_11_out, T4);
  not not_12 (not_12_out, EMERG);
  not not_13 (not_13_out, S2);
  not not_14 (not_14_out, S1);
  not not_15 (not_15_out, S0);
  not not_16 (not_16_out, EMERG);
  not not_17 (not_17_out, S2);
  not not_18 (not_18_out, S1);
  not not_19 (not_19_out, T2);
  not not_20 (not_20_out, EMERG);
  not not_21 (not_21_out, S2);
  not not_22 (not_22_out, S0);
  not not_23 (not_23_out, EMERG);
  not not_24 (not_24_out, S2);
  not not_25 (not_25_out, T4);
  not not_26 (not_26_out, EMERG);
  or or_1 (N2, and_1_out, and_2_out);
  and and_3 (and_3_out, not_4_out, not_5_out, S0, T2, not_6_out);
  or or_2 (N1, and_3_out, and_4_out, and_5_out);
  and and_4 (and_4_out, not_7_out, S1, not_8_out, not_9_out);
  and and_5 (and_5_out, not_10_out, S1, not_11_out, not_12_out);
  and and_6 (and_6_out, not_13_out, not_14_out, not_15_out, T1, not_16_out);
  and and_7 (and_7_out, not_17_out, not_18_out, S0, not_19_out, not_20_out);
  and and_8 (and_8_out, not_21_out, S1, not_22_out, T3, not_23_out);
  and and_9 (and_9_out, not_24_out, S1, S0, not_25_out, not_26_out);
  or or_3 (N0, and_6_out, and_7_out, and_8_out, and_9_out);
endmodule

// 输出函数
module \红绿灯状态输出函数_真值表  (
  input  S2,
  input  S1,
  input  S0,
  output R1,
  output Y1,
  output G1,
  output R2,
  output Y2,
  output G2,
  output PASS1,
  output PASS2
);

  wire and_1_out, and_2_out, and_5_out, and_6_out, not_1_out, not_2_out, not_3_out, not_4_out, not_5_out,
       not_6_out, not_7_out, not_8_out, not_9_out, not_10_out, not_11_out, not_12_out, not_13_out,
       not_14_out, not_15_out, not_16_out, not_17_out, not_18_out;

  not not_1 (not_1_out, S2);
  not not_2 (not_2_out, S1);
  not not_3 (not_3_out, S0);
  not not_4 (not_4_out, S2);
  not not_5 (not_5_out, S1);
  not not_6 (not_6_out, S2);
  not not_7 (not_7_out, S1);
  not not_8 (not_8_out, S0);
  not not_9 (not_9_out, S2);
  not not_10 (not_10_out, S1);
  not not_11 (not_11_out, S1);
  not not_12 (not_12_out, S0);
  not not_13 (not_13_out, S2);
  not not_14 (not_14_out, S2);
  not not_15 (not_15_out, S0);
  not not_16 (not_16_out, S2);
  not not_17 (not_17_out, S1);
  not not_18 (not_18_out, S2);
  and and_1 (and_1_out, not_1_out, S1);
  and and_2 (and_2_out, S2, not_2_out, not_3_out);
  and and_3 (Y1, not_4_out, not_5_out, S0);
  and and_4 (G1, not_6_out, not_7_out, not_8_out);
  and and_5 (and_5_out, not_9_out, not_10_out);
  and and_6 (and_6_out, not_11_out, not_12_out);
  and and_7 (Y2, not_13_out, S1, S0);
  and and_8 (G2, not_14_out, S1, not_15_out);
  and and_9 (PASS1, not_16_out, not_17_out);
  and and_10 (PASS2, not_18_out, S1);
  or or_1 (R1, and_1_out, and_2_out);
  or or_2 (R2, and_5_out, and_6_out);
endmodule

module \红绿灯  (
  input  in_1,
  output R1,
  output Y1,
  output [2:0] Status,
  output G1,
  output R2,
  output Y2,
  output [7:0] Timer,
  output G2
);

  wire CLK, not_1_out, or_1_out, or_3_out, PASS1, PASS2, RST, T1, T2, T3, T4, Y1c, Y2c, \紧急开关_p1 , \紧急开关_p3 ,
       \紧急开关_p4 , \紧急情况 ;
  wire [2:0] S1B, S2B, \红绿灯状态机_自动生成_1_n0 ;
  wire [3:0] S1T, S2T;
  wire [7:0] counter_1_q, Timer1, Timer2;

  LED #(.active("true")) led_1 (.in(R1));
  LED #(.active("true")) led_2 (.in(Y1c));
  LED #(.active("true")) led_3 (.in(G1));
  or or_1 (or_1_out, T4, RST);
  _7_Segment_Display #(.active("true")) u_7_segment_display_1 (
    .g(S1T[0]), .f(S1T[1]), .a(S1T[2]), .b(S1T[3]), .e(S1B[0]), .d(S1B[1]), .c(S1B[2]));  // open: dp
  _7_Segment_Display #(.active("true")) u_7_segment_display_2 (
    .g(S2T[0]), .f(S2T[1]), .a(S2T[2]), .b(S2T[3]), .e(S2B[0]), .d(S2B[1]), .c(S2B[2]));  // open: dp
  Register #(.width(3), .trigger("rising"), .Select("low")) \u_状态  (
    .D(\红绿灯状态机_自动生成_1_n0 ), .Q(Status), .clk(CLK));  // open: en, clr
  \双位十进制双向计数器  \u_双位十进制双向计数器_1  (
    .CLK(CLK), .\使能 (PASS1), .\异步置位控制 (or_1_out), .\异步预置 (8'h20), .\Mode_0正计数_1倒计数 (1'b1), .Q(Timer1));  // open: 进位_借位
  // DipSwitch #(.NSwitches(1)) 紧急开关: pin names not known; wires that end beside it: \紧急开关_p1 , \紧急开关_p1 , \紧急开关_p3 , \紧急开关_p4 , \紧急开关_p4 
  // Probe on Timer1
  LED #(.active("true")) led_4 (.in(R2));
  LED #(.active("true")) led_5 (.in(Y2c));
  LED #(.active("true")) led_6 (.in(G2));
  or or_2 (\紧急情况 , in_1, \紧急开关_p3 );
  \红绿灯状态输出函数_真值表  \u_红绿灯状态输出函数_真值表_1  (
    .S2(Status[2]), .R1(R1), .S1(Status[1]), .S0(Status[0]), .Y1(Y1), .G1(G1), .R2(R2), .Y2(Y2), .G2(G2),
    .PASS1(PASS1), .PASS2(PASS2));
  \红绿灯状态机_自动生成  \u_红绿灯状态机_自动生成_1  (
    .S2(Status[2]), .N2(\红绿灯状态机_自动生成_1_n0 [2]), .S1(Status[1]), .S0(Status[0]), .T1(T1), .T2(T2), .T3(T3),
    .N1(\红绿灯状态机_自动生成_1_n0 [1]), .T4(T4), .EMERG(\紧急情况 ), .N0(\红绿灯状态机_自动生成_1_n0 [0]));
  \_8位无符号比较器  \u_8位无符号比较器_1  (.X(Timer1), .Y(8'h4), .Equal(T1));  // open: Great, Less
  \_8位无符号比较器  \u_8位无符号比较器_2  (.X(Timer1), .Y(8'h1), .Equal(T2));  // open: Great, Less
  or or_3 (or_3_out, T2, RST);
  \双位十进制双向计数器  \u_双位十进制双向计数器_2  (
    .CLK(CLK), .\使能 (PASS2), .\异步置位控制 (or_3_out), .\异步预置 (8'h10), .\Mode_0正计数_1倒计数 (1'b1), .Q(Timer2));  // open: 进位_借位
  // Probe on Timer2
  and and_1 (Y1c, Y1, CLK);
  and and_2 (Y2c, Y2, CLK);
  not not_1 (not_1_out, \紧急情况 );
  Clock #(.highDuration(1), .lowDuration(1)) clock_1 (.out(CLK));
  \_2路选择器_8位  \u_2路选择器_8位_1  (.X(Timer1), .Sel(PASS2), .Y(Timer2), .Out(Timer));
  \_8位无符号比较器  \u_8位无符号比较器_3  (.X(Timer2), .Y(8'h4), .Equal(T3));  // open: Great, Less
  \_8位无符号比较器  \u_8位无符号比较器_4  (.X(Timer2), .Y(8'h1), .Equal(T4));  // open: Great, Less
  D_Flip_Flop #(.trigger("rising"), .Pre_Clr_Positions("LEGACY"), .NegatePresetClear("false"), .enable("true"), .NewFFLayout("false")) d_ff_1 (
    .clk(CLK), .D(not_1_out), .Qn(RST));  // open: Q, preset, en, reset
  Counter #(.width(8), .max('hff), .ongoal("wrap"), .trigger("rising"), .behavior("new")) counter_1 (
    .Q(counter_1_q), .clk(CLK));  // open: load, D, count, carry, clr, preset, down
  // Probe on counter_1_q
  \数码管驱动  \u_数码管驱动_1  (
    .X3(Timer[7]), .X2(Timer[6]), .Seg_1(S2T[0]), .X1(Timer[5]), .X0(Timer[4]), .Seg_2(S2T[1]),
    .Seg_3(S2T[2]), .Seg_4(S2T[3]), .Seg_5(S2B[0]), .Seg_6(S2B[1]), .Seg_7(S2B[2]));
  \数码管驱动  \u_数码管驱动_2  (
    .X3(Timer[3]), .X2(Timer[2]), .Seg_1(S1T[0]), .X1(Timer[1]), .X0(Timer[0]), .Seg_2(S1T[1]),
    .Seg_3(S1T[2]), .Seg_4(S1T[3]), .Seg_5(S1B[0]), .Seg_6(S1B[1]), .Seg_7(S1B[2]));

  // Other names for the same wires on the sheet: E = in_1

  // Notes on the sheet:
  //   主道红绿灯
  //   测试时要求主道20秒，辅道10秒
  //   倒计时
  //   状态机现态
  //   主道计时逻辑
  //   辅道红绿灯
  //   状态机现态
  //   当前倒计时
  //   引脚区，用于EduCoder测试
  //   辅道计时逻辑
  //   控制黄灯闪烁
  //   初始化信号，第一拍为1
  //   用于预置计数器初始值
  //   当前倒计时
  //   时钟计数
endmodule
